// Logisim project circuito_lab1.circ as structural Verilog: 1 circuit, main circuit main
module main (
  input  REG_DEST,
  input  habilitaGrav,
  input  R___0
);

  wire CLK, registerfile_1_p7;
  wire [4:0] rA, rB, rW;
  wire [31:0] adder_1_out, bit_extender_1_out, mipsprogramrom_1_p2, multiplexer_2_out, register_1_q,
       registerfile_1_p8, W;

  Register #(.width(32)) register_1 (.D(adder_1_out), .Q(register_1_q), .clk(CLK));  // open: en, clr
  Adder #(.width(32)) adder_1 (.a(register_1_q), .b(32'h4), .out(adder_1_out));  // open: cin, cout
  // MIPSProgramROM mipsprogramrom_1: pin names not known; wires that end beside it: register_1_q, {mipsprogramrom_1_p2[31:26], rA, rB, mipsprogramrom_1_p2[15:0]}
  Multiplexer #(.width(5)) multiplexer_1 (
    .in0(mipsprogramrom_1_p2[15:11]), .in1(rB), .out(rW), .sel(REG_DEST));  // open: en
  assign bit_extender_1_out = {{16{1'b0}}, mipsprogramrom_1_p2[15:0]};  // Bit_Extender bit_extender_1
  Clock clock_1 (.out(CLK));
  // RegisterFile registerfile_1: pin names not known; wires that end beside it: W, CLK, habilitaGrav, rW, rA, rB, registerfile_1_p7, registerfile_1_p8
  Multiplexer #(.width(32)) multiplexer_2 (
    .in0(registerfile_1_p8), .in1(bit_extender_1_out), .out(multiplexer_2_out), .sel(R___0));  // open: en
  // Mips_ALU mips_alu_1: pin names not known; wires that end beside it: registerfile_1_p7, multiplexer_2_out, 4'b0010, W

  // Notes on the sheet:
  //   Tipo I
  //   Tipo R
  //   R
  //   I
  //   Destino
  //   I - 1
  //   Tipo de OP
endmodule
