// Logisim project registrador4bits.circ as structural Verilog: 1 circuit, main circuit main
module main (
  input  [3:0] D,
  input  En,
  output [3:0] Q
);

  wire Clk_out;

  Clock Clk (.out(Clk_out));
  Register #(.width(1)) _3 (.D(D[3]), .en(En), .Q(Q[3]), .clk(Clk_out), .clr(1'b0));
  Register #(.width(1)) _2 (.D(D[2]), .en(En), .Q(Q[2]), .clk(Clk_out), .clr(1'b0));
  Register #(.width(1)) _0 (.D(D[0]), .en(En), .Q(Q[0]), .clk(Clk_out), .clr(1'b0));
  Register #(.width(1)) _1 (.D(D[1]), .en(En), .Q(Q[1]), .clk(Clk_out), .clr(1'b0));

  // Notes on the sheet:
  //   Clr
endmodule
