// Logisim project projeto_ula.circ as structural Verilog: 6 circuits, main circuit main
module main (
  input  [7:0] A,
  input  [7:0] B,
  input  [3:0] OP_CODE,
  output [7:0] S
);

  // ULA ula_1: pin names not known; wires that end beside it: A, B, OP_CODE, S
endmodule

module ULA (
  input  [7:0] A,
  input  [7:0] B,
  input  [3:0] OP_CODE,
  input  [7:0] Cin,
  input  [7:0] Vin,
  output [7:0] S,
  output [7:0] Cout,
  output [7:0] Vout
);

  wire [7:0] ADD, AND, DES__DIR, DES__ESQ, MULTI, NAND, NOR, NOT, OR, SUB, undriven, undriven_2, undriven_3,
       XNOR, XOR;

  assign AND = A & B;  // AND_Gate and_1, 8 bits wide
  assign OR = A | B;  // OR_Gate or_1, 8 bits wide
  assign NOT = ~A;  // NOT_Gate not_1, 8 bits wide
  assign XOR = A ^ B;  // XOR_Gate xor_1, 8 bits wide
  assign NOR = ~(A | B);  // NOR_Gate nor_1, 8 bits wide
  assign NAND = ~(A & B);  // NAND_Gate nand_1, 8 bits wide
  assign XNOR = ~(A ^ B);  // XNOR_Gate xnor_1, 8 bits wide
  Multiplier multiplier_1 (.a(A), .b(B), .out(MULTI));  // open: cin, cout
  Shifter shifter_1 (.in(A), .\dist (3'b100), .out(DES__ESQ));
  Shifter #(.shift("lr")) shifter_2 (.in(A), .\dist (3'b100), .out(DES__DIR));
  somadorCompleto somadorcompleto_1 (.A(A), .B(B), .Cin(Cin), .S(ADD), .Cout(Cout));
  subtratorCompleto subtratorcompleto_1 (.A(A), .B(B), .Vin(Vin), .S(SUB), .Vout(Vout));
  Multiplexer #(.select(4), .width(8)) multiplexer_1 (
    .in1(XNOR), .in2(OR), .in3(DES__DIR), .in4(XOR), .in5(MULTI), .in6(NOR), .in7(AND), .in8(undriven),
    .in9(SUB), .in10(DES__ESQ), .in11(NAND), .in12(NOT), .in13(undriven_2), .in14(undriven_3), .in15(ADD),
    .out(S), .sel(OP_CODE));  // open: in0, en
endmodule

// 1/2S
module meioSomador (
  input  [7:0] A,
  input  [7:0] B,
  output [7:0] S,
  output [7:0] C
);

  assign C = A & B;  // AND_Gate AND, 8 bits wide
  assign S = A ^ B;  // XOR_Gate XOR, 8 bits wide
endmodule

// S
module somadorCompleto (
  input  [7:0] A,
  input  [7:0] B,
  input  [7:0] Cin,
  output [7:0] S,
  output [7:0] Cout
);

  wire [7:0] meiosomador_1_c, meiosomador_1_s, meiosomador_2_c;

  meioSomador meiosomador_1 (.A(A), .B(B), .S(meiosomador_1_s), .C(meiosomador_1_c));
  meioSomador meiosomador_2 (.A(meiosomador_1_s), .B(Cin), .S(S), .C(meiosomador_2_c));
  assign Cout = meiosomador_1_c | meiosomador_2_c;  // OR_Gate or_1, 8 bits wide
endmodule

// 1/2M
module meioSubtrator (
  input  [7:0] A,
  input  [7:0] B,
  output [7:0] S,
  output [7:0] Vout
);

  assign S = A ^ B;  // XOR_Gate xor_1, 8 bits wide
  assign Vout = ~A & B;  // AND_Gate and_1, 8 bits wide
endmodule

// M
module subtratorCompleto (
  input  [7:0] A,
  input  [7:0] B,
  input  [7:0] Vin,
  output [7:0] S,
  output [7:0] Vout
);

  wire [7:0] and_1_out, and_2_out, meiosubtrator_1_s, meiosubtrator_1_vout;

  meioSubtrator meiosubtrator_1 (.A(A), .B(B), .S(meiosubtrator_1_s), .Vout(meiosubtrator_1_vout));
  assign and_1_out = B & Vin;  // AND_Gate and_1, 8 bits wide
  assign and_2_out = ~A & Vin;  // AND_Gate and_2, 8 bits wide
  assign S = meiosubtrator_1_s ^ Vin;  // XOR_Gate xor_1, 8 bits wide
  assign Vout = and_2_out | meiosubtrator_1_vout | and_1_out;  // OR_Gate or_1, 8 bits wide
endmodule
