// Logisim project projeto_ula_FEL.circ as structural Verilog: 8 circuits, main circuit ULA
module main (
  input  [7:0] A,
  input  [7:0] B,
  input  Bin,
  input  [3:0] OP_CODE,
  input  Cin,
  output [7:0] S,
  output Cout,
  output Bout
);

  ULA ula_1 (.A(A), .B(B), .Cin(Cin), .Bin(Bin), .Bout(Bout), .S(S), .OP_CODE(OP_CODE), .Cout(Cout));
endmodule

module ULA (
  input  [7:0] A,
  input  [7:0] B,
  input  [3:0] OP_CODE,
  input  Bin,
  input  Cin,
  output [7:0] S,
  output Bout,
  output Cout
);

  wire [7:0] ADD, AND, DES__DIR, DES__ESQ, MULTI, NAND, NOR, NOT, OR, SUB, XNOR, XOR;

  assign AND = A & B;  // AND_Gate and_1, 8 bits wide
  assign OR = A | B;  // OR_Gate or_1, 8 bits wide
  assign NOT = ~A;  // NOT_Gate not_1, 8 bits wide
  assign XOR = A ^ B;  // XOR_Gate xor_1, 8 bits wide
  assign NOR = ~(A | B);  // NOR_Gate nor_1, 8 bits wide
  assign NAND = ~(A & B);  // NAND_Gate nand_1, 8 bits wide
  assign XNOR = ~(A ^ B);  // XNOR_Gate xnor_1, 8 bits wide
  Multiplier multiplier_1 (.a(A), .b(B), .out(MULTI));  // open: cin, cout
  Shifter shifter_1 (.in(A), .\dist (3'b100), .out(DES__ESQ));
  Shifter #(.shift("lr")) shifter_2 (.in(A), .\dist (3'b100), .out(DES__DIR));
  subtrator8bits subtrator8bits_1 (.Bin(Bin), .A(A), .B(B), .D(SUB), .Bout(Bout));
  somador8bits somador8bits_1 (.Cin(Cin), .A(A), .out_4(ADD), .Cout(Cout), .B(B));
  Multiplexer #(.select(4), .width(8)) multiplexer_1 (
    .in1(XNOR), .in2(OR), .in3(DES__DIR), .in4(XOR), .in5(MULTI), .in6(NOR), .in7(AND), .in9(SUB),
    .in10(DES__ESQ), .in11(NAND), .in12(NOT), .in15(ADD), .out(S), .sel(OP_CODE));  // open: in0, in8, in13, in14, en

  // Notes on the sheet:
  //   ADIÇÃO
  //   SUBTRAÇÃO
endmodule

// 1/2S
module meioSomador (
  input  A,
  input  B,
  output S,
  output C
);

  and AND (C, A, B);
  xor XOR (S, A, B);
endmodule

// S
module somadorCompleto (
  input  A,
  input  B,
  input  Cin,
  output S,
  output Cout
);

  wire meiosomador_1_c, meiosomador_1_s, meiosomador_2_c;

  meioSomador meiosomador_1 (.A(A), .B(B), .S(meiosomador_1_s), .C(meiosomador_1_c));
  meioSomador meiosomador_2 (.A(meiosomador_1_s), .B(Cin), .S(S), .C(meiosomador_2_c));
  or or_1 (Cout, meiosomador_1_c, meiosomador_2_c);
endmodule

// 1/2M
module meioSubtrator (
  input  A,
  input  B,
  output D,
  output Bout
);

  xor xor_1 (D, A, B);
  and and_1 (Bout, ~A, B);  // AND_Gate
endmodule

// M
module subtratorCompleto (
  input  A,
  input  B,
  input  Bin,
  output D,
  output Bout
);

  wire and_1_out, and_2_out, meiosubtrator_1_bout, meiosubtrator_1_d;

  meioSubtrator meiosubtrator_1 (.A(A), .B(B), .D(meiosubtrator_1_d), .Bout(meiosubtrator_1_bout));
  and and_1 (and_1_out, B, Bin);
  and and_2 (and_2_out, ~A, Bin);  // AND_Gate
  xor xor_1 (D, meiosubtrator_1_d, Bin);
  or or_1 (Bout, and_2_out, meiosubtrator_1_bout, and_1_out);
endmodule

// S8bits
module somador8bits (
  input  [7:0] A,
  input  Cin,
  input  [7:0] B,
  output [7:0] out_4,
  output Cout
);

  wire somadorcompleto_1_cout, somadorcompleto_2_cout, somadorcompleto_3_cout, somadorcompleto_4_cout,
       somadorcompleto_5_cout, somadorcompleto_6_cout, somadorcompleto_7_cout;

  somadorCompleto somadorcompleto_1 (.A(A[0]), .B(B[0]), .Cin(Cin), .S(out_4[0]), .Cout(somadorcompleto_1_cout));
  somadorCompleto somadorcompleto_2 (
    .A(A[1]), .B(B[1]), .Cin(somadorcompleto_1_cout), .S(out_4[1]), .Cout(somadorcompleto_2_cout));
  somadorCompleto somadorcompleto_3 (
    .A(A[3]), .B(B[3]), .Cin(somadorcompleto_4_cout), .S(out_4[3]), .Cout(somadorcompleto_3_cout));
  somadorCompleto somadorcompleto_4 (
    .A(A[2]), .B(B[2]), .Cin(somadorcompleto_2_cout), .S(out_4[2]), .Cout(somadorcompleto_4_cout));
  somadorCompleto somadorcompleto_5 (
    .A(A[4]), .B(B[4]), .Cin(somadorcompleto_3_cout), .S(out_4[4]), .Cout(somadorcompleto_5_cout));
  somadorCompleto somadorcompleto_6 (
    .A(A[5]), .B(B[5]), .Cin(somadorcompleto_5_cout), .S(out_4[5]), .Cout(somadorcompleto_6_cout));
  somadorCompleto somadorcompleto_7 (
    .A(A[6]), .B(B[6]), .Cin(somadorcompleto_6_cout), .S(out_4[6]), .Cout(somadorcompleto_7_cout));
  somadorCompleto somadorcompleto_8 (.A(A[7]), .B(B[7]), .Cin(somadorcompleto_7_cout), .S(out_4[7]), .Cout(Cout));
endmodule

// M8bits
module subtrator8bits (
  input  [7:0] A,
  input  Bin,
  input  [7:0] B,
  output [7:0] D,
  output Bout
);

  wire subtratorcompleto_1_bout, subtratorcompleto_2_bout, subtratorcompleto_3_bout,
       subtratorcompleto_4_bout, subtratorcompleto_5_bout, subtratorcompleto_6_bout, subtratorcompleto_7_bout;

  subtratorCompleto subtratorcompleto_1 (.A(A[0]), .B(B[0]), .Bin(Bin), .D(D[0]), .Bout(subtratorcompleto_1_bout));
  subtratorCompleto subtratorcompleto_2 (
    .A(A[1]), .B(B[1]), .Bin(subtratorcompleto_1_bout), .D(D[1]), .Bout(subtratorcompleto_2_bout));
  subtratorCompleto subtratorcompleto_3 (
    .A(A[3]), .B(B[3]), .Bin(subtratorcompleto_4_bout), .D(D[3]), .Bout(subtratorcompleto_3_bout));
  subtratorCompleto subtratorcompleto_4 (
    .A(A[2]), .B(B[2]), .Bin(subtratorcompleto_2_bout), .D(D[2]), .Bout(subtratorcompleto_4_bout));
  subtratorCompleto subtratorcompleto_5 (
    .A(A[4]), .B(B[4]), .Bin(subtratorcompleto_3_bout), .D(D[4]), .Bout(subtratorcompleto_5_bout));
  subtratorCompleto subtratorcompleto_6 (
    .A(A[5]), .B(B[5]), .Bin(subtratorcompleto_5_bout), .D(D[5]), .Bout(subtratorcompleto_6_bout));
  subtratorCompleto subtratorcompleto_7 (
    .A(A[6]), .B(B[6]), .Bin(subtratorcompleto_6_bout), .D(D[6]), .Bout(subtratorcompleto_7_bout));
  subtratorCompleto subtratorcompleto_8 (.A(A[7]), .B(B[7]), .Bin(subtratorcompleto_7_bout), .D(D[7]), .Bout(Bout));
endmodule
