// Logisim project somador2bits.circ as structural Verilog: 3 circuits, main circuit main
module main (
  input  A1,
  input  B1,
  input  A2,
  input  B2,
  input  Cin,
  output S1,
  output S2,
  output Cout
);

  wire somadorcompleto_1_cout;

  somadorCompleto somadorcompleto_1 (.A(A1), .B(B1), .Cin(Cin), .S(S1), .Cout(somadorcompleto_1_cout));
  somadorCompleto somadorcompleto_2 (.A(A2), .B(B2), .Cin(somadorcompleto_1_cout), .S(S2), .Cout(Cout));
endmodule

// h +
module meioSomador (
  input  A,
  input  B,
  output S,
  output C
);

  and and_1 (C, A, B);
  xor xor_1 (S, A, B);
endmodule

module somadorCompleto (
  input  A,
  input  B,
  input  Cin,
  output S,
  output Cout
);

  wire meiosomador_1_c, meiosomador_1_s, meiosomador_2_c;

  meioSomador meiosomador_1 (.A(A), .B(B), .S(meiosomador_1_s), .C(meiosomador_1_c));
  meioSomador meiosomador_2 (.A(meiosomador_1_s), .B(Cin), .S(S), .C(meiosomador_2_c));
  or or_1 (Cout, meiosomador_1_c, meiosomador_2_c);
endmodule
