// Logisim project aula1.circ as structural Verilog: 1 circuit, main circuit main
module main (
  input  [31:0] Dado_a_ser_gravado,
  input  habilitaGrav,
  input  [4:0] ORIGEM2,
  input  [4:0] regDestino,
  input  [4:0] ORIGEM1,
  output [31:0] Saida_da_origem_1,
  output [31:0] Saida_da_origem_2
);

  wire CLK_out;

  Clock CLK (.out(CLK_out));
  // RegisterFile registerfile_1: pin names not known; wires that end beside it: Dado_a_ser_gravado, CLK_out, habilitaGrav, regDestino, ORIGEM1, ORIGEM2, Saida_da_origem_1, Saida_da_origem_2

  // Notes on the sheet:
  //   Dado_a_ser_gravado: pull=west
endmodule
