// Logisim project circuito_aula1.circ as structural Verilog: 1 circuit, main circuit main
module main (
  input  [3:0] ALU_OP,
  input  habilitaGrav,
  output [5:0] FUNCT,
  output [4:0] SHAMT,
  output [4:0] DESTINO,
  output [4:0] ORIGEM2,
  output [4:0] ORIGEM1,
  output [5:0] OPCODE
);

  wire CLK, registerfile_1_p1, registerfile_1_p7, registerfile_1_p8;
  wire [31:0] adder_1_out, register_1_q;

  Clock clock_1 (.out(CLK));
  Register #(.width(32)) register_1 (.D(adder_1_out), .Q(register_1_q), .clk(CLK));  // open: en, clr
  Adder #(.width(32)) adder_1 (.a(register_1_q), .b(32'h4), .out(adder_1_out));  // open: cin, cout
  // MIPSProgramROM mipsprogramrom_1: pin names not known; wires that end beside it: register_1_q, {OPCODE, ORIGEM1, ORIGEM2, DESTINO, SHAMT, FUNCT}
  // RegisterFile registerfile_1: pin names not known; wires that end beside it: registerfile_1_p1, CLK, habilitaGrav, DESTINO, ORIGEM1, ORIGEM2, registerfile_1_p7, registerfile_1_p8
  // Mips_ALU mips_alu_1: pin names not known; wires that end beside it: registerfile_1_p7, registerfile_1_p8, ALU_OP, registerfile_1_p1

  // Notes on the sheet:
  //   Opcode | Origem1 | Origem2 | Destino | Shamt | Funct
  //   ADD - 001x com x - >náo importa
endmodule
