// Logisim project circuito_aula2.circ as structural Verilog: 1 circuit, main circuit main
module main (
  input  MEM_TO_REG,
  input  REG_DEST,
  input  STORE,
  input  in_4,
  input  [3:0] ALU_OP,
  input  habilitaGrav,
  input  ALU_SOURCE
);

  wire CLK, clock_2_out, registerfile_1_p7;
  wire [4:0] mipsprogramrom_1_p2_2, multiplexer_1_out;
  wire [31:0] adder_1_out, bit_extender_1_out, mips_alu_1_p4, mips_ram_1_p5, mipsprogramrom_1_p2,
       multiplexer_3_out, register_1_q, registerfile_1_p1, registerfile_1_p8;

  Adder #(.width(32)) adder_1 (.a(register_1_q), .b(32'h4), .out(adder_1_out));  // open: cin, cout
  Register #(.width(32)) register_1 (.D(adder_1_out), .Q(register_1_q), .clk(CLK));  // open: en, clr
  // MIPSProgramROM mipsprogramrom_1: pin names not known; wires that end beside it: register_1_q, {mipsprogramrom_1_p2[31:21], mipsprogramrom_1_p2_2, mipsprogramrom_1_p2[15:0]}
  Multiplexer #(.width(5)) multiplexer_1 (
    .in0(mipsprogramrom_1_p2[15:11]), .in1(mipsprogramrom_1_p2_2), .out(multiplexer_1_out), .sel(REG_DEST));  // open: en
  Clock clock_1 (.out(CLK));
  assign bit_extender_1_out = {{16{1'b0}}, mipsprogramrom_1_p2[15:0]};  // Bit_Extender bit_extender_1
  // RegisterFile registerfile_1: pin names not known; wires that end beside it: registerfile_1_p1, CLK, habilitaGrav, multiplexer_1_out, mipsprogramrom_1_p2[25:21], mipsprogramrom_1_p2_2, registerfile_1_p7, registerfile_1_p8
  Multiplexer #(.width(32)) multiplexer_2 (
    .in0(mips_alu_1_p4), .in1(mips_ram_1_p5), .out(registerfile_1_p1), .en(MEM_TO_REG));  // open: sel
  Multiplexer #(.width(32)) multiplexer_3 (
    .in0(registerfile_1_p8), .in1(bit_extender_1_out), .out(multiplexer_3_out), .sel(ALU_SOURCE));  // open: en
  // Mips_ALU mips_alu_1: pin names not known; wires that end beside it: registerfile_1_p7, multiplexer_3_out, ALU_OP, mips_alu_1_p4, registerfile_1_p8
  Clock clock_2 (.out(clock_2_out));
  // MIPS_RAM mips_ram_1: pin names not known; wires that end beside it: mips_alu_1_p4[19:0], STORE, clock_2_out, in_4, mips_ram_1_p5

  // Notes on the sheet:
  //   Tipo I
  //   Tipo R
  //   R
  //   I
  //   Primeira Origem
  //   Segunda Origem
  //   Destino
  //   Estender bits (Imediato)
  //   LOAD
  //   20b de end
  //   QntMemoria = 2^#end = 2^20 * 4(bytes) = 4MB
endmodule
