// Logisim project circuito_aula3.circ as structural Verilog: 1 circuit, main circuit main
module main (
  input  in_1,
  input  in_2,
  input  in_3,
  input  in_4,
  input  in_5,
  input  in_6,
  input  [3:0] in_7,
  input  in_8
);

  wire CLK, registerfile_1_p7;
  wire [4:0] mipsprogramrom_1_p2_2, multiplexer_1_out;
  wire [31:0] adder_1_out, bit_extender_1_out, mips_alu_1_p4, mips_ram_1_p6, mipsprogramrom_1_p2,
       multiplexer_3_out, register_1_q, registerfile_1_p1, registerfile_1_p8;

  Adder #(.width(32)) adder_1 (.a(register_1_q), .b(32'h4), .out(adder_1_out));  // open: cin, cout
  Register #(.width(32)) register_1 (.D(adder_1_out), .Q(register_1_q), .clk(CLK));  // open: en, clr
  Clock clock_1 (.out(CLK));
  // MIPSProgramROM mipsprogramrom_1: pin names not known; wires that end beside it: register_1_q, {mipsprogramrom_1_p2[31:21], mipsprogramrom_1_p2_2, mipsprogramrom_1_p2[15:0]}
  Multiplexer #(.width(5)) multiplexer_1 (
    .in0(mipsprogramrom_1_p2[15:11]), .in1(mipsprogramrom_1_p2_2), .out(multiplexer_1_out), .sel(in_1));  // open: en
  assign bit_extender_1_out = {{16{1'b0}}, mipsprogramrom_1_p2[15:0]};  // Bit_Extender bit_extender_1
  // RegisterFile registerfile_1: pin names not known; wires that end beside it: registerfile_1_p1, CLK, in_3, multiplexer_1_out, mipsprogramrom_1_p2[25:21], mipsprogramrom_1_p2_2, registerfile_1_p7, registerfile_1_p8
  Multiplexer #(.width(32)) multiplexer_2 (
    .in0(mips_alu_1_p4), .in1(mips_ram_1_p6), .out(registerfile_1_p1), .sel(in_2));  // open: en
  Multiplexer #(.width(32)) multiplexer_3 (
    .in0(registerfile_1_p8), .in1(bit_extender_1_out), .out(multiplexer_3_out), .sel(in_5));  // open: en
  // Mips_ALU mips_alu_1: pin names not known; wires that end beside it: registerfile_1_p7, multiplexer_3_out, in_7, mips_alu_1_p4, registerfile_1_p8
  // MIPS_RAM mips_ram_1: pin names not known; wires that end beside it: mips_alu_1_p4[19:0], in_6, CLK, in_4, in_8, mips_ram_1_p6

  // Other names for the same wires on the sheet: ALU_OP[3:0] = in_7; ALU_SRC = in_5; LOAD = in_4; MEM_TO_REG = in_2;
  //   REG_DEST = in_1; REG_W = in_3; RESET = in_8; STORE = in_6

  // Notes on the sheet:
  //   STORE e LOAD do tipo I (ativar ALU_SRC e REG_DEST)
  //   Tipo I
  //   Tipo R
  //   R
  //   I
  //   Primeira Origem
  //   Segunda Origem
  //   Destino
  //   Estender bits (Imediato)
  //   LOAD
  //   20b de end
  //   QntMemoria = 2^#end = 2^20 * 4(bytes) = 4MB
endmodule
