// Logisim project circuito_aula4.circ as structural Verilog: 1 circuit, main circuit main
module main (
  input  [3:0] in_1
);

  wire addf_out, ADDI, ADDU, ALU_SRC, CLK, F0, F1, F2, F3, F4, F5, OP0, OP1, OP2, OP3, OP4, OP5, REG_W,
       registerfile_1_p7, STORE, subf_out, SUBU, Zero_2_out, Zero_out;
  wire [4:0] mipsprogramrom_1_p2_2, multiplexer_1_out;
  wire [20:6] mipsprogramrom_1_p2;
  wire [31:0] adder_1_out, bit_extender_1_out, mips_alu_1_p4, mips_ram_1_p6, multiplexer_3_out, register_1_q,
       registerfile_1_p1, registerfile_1_p8;

  and and_1 (STORE, OP0, OP1, ~OP2, OP3, ~OP4, OP5);  // AND_Gate
  and Zero (Zero_out, ~OP0, ~OP1, ~OP2, ~OP3, ~OP4, ~OP5);  // AND_Gate
  and subf (subf_out, F0, F1, ~F2, ~F3, ~F4, F5);  // AND_Gate
  Register #(.width(32)) register_1 (.D(adder_1_out), .Q(register_1_q), .clk(CLK));  // open: en, clr
  Adder #(.width(32)) adder_1 (.a(register_1_q), .b(32'h4), .out(adder_1_out));  // open: cin, cout
  and and_2 (SUBU, Zero_out, subf_out);
  and and_3 (ADDI, OP0, ~OP1, ~OP2, OP3, ~OP4, ~OP5);  // AND_Gate
  and Zero_2 (Zero_2_out, ~OP0, ~OP1, ~OP2, ~OP3, ~OP4, ~OP5);  // AND_Gate
  and addf (addf_out, F0, ~F1, ~F2, ~F3, ~F4, F5);  // AND_Gate
  // MIPSProgramROM mipsprogramrom_1: pin names not known; wires that end beside it: register_1_q, {OP5, OP4, OP3, OP2, OP1, OP0, mipsprogramrom_1_p2_2, mipsprogramrom_1_p2, F5, F4, F3, F2, F1, F0}
  and and_4 (ADDU, Zero_2_out, addf_out);
  or or_1 (ALU_SRC, STORE, ADDI);
  or or_2 (REG_W, ADDI, ADDU, SUBU);
  Multiplexer #(.width(5)) multiplexer_1 (
    .in0(mipsprogramrom_1_p2[15:11]), .in1(mipsprogramrom_1_p2[20:16]), .out(multiplexer_1_out), .sel(ALU_SRC));  // open: en
  Clock clock_1 (.out(CLK));
  assign bit_extender_1_out = {{16{1'b0}}, {mipsprogramrom_1_p2[15:6], F5, F4, F3, F2, F1, F0}};  // Bit_Extender bit_extender_1
  // RegisterFile registerfile_1: pin names not known; wires that end beside it: registerfile_1_p1, CLK, REG_W, multiplexer_1_out, mipsprogramrom_1_p2_2, mipsprogramrom_1_p2[20:16], registerfile_1_p7, registerfile_1_p8
  Multiplexer #(.width(32)) multiplexer_2 (
    .in0(mips_alu_1_p4), .in1(mips_ram_1_p6), .out(registerfile_1_p1), .sel(1'b0));  // open: en
  Multiplexer #(.width(32)) multiplexer_3 (
    .in0(registerfile_1_p8), .in1(bit_extender_1_out), .out(multiplexer_3_out), .sel(ALU_SRC));  // open: en
  // Mips_ALU mips_alu_1: pin names not known; wires that end beside it: registerfile_1_p7, multiplexer_3_out, in_1, mips_alu_1_p4, registerfile_1_p8
  // MIPS_RAM mips_ram_1: pin names not known; wires that end beside it: mips_alu_1_p4[19:0], STORE, CLK, 1'b0, 1'b0, mips_ram_1_p6

  // Other names for the same wires on the sheet: FUNCT[5:0] = {F5, F4, F3, F2, F1, F0};
  //   OPCODE[5:0] = {OP5, OP4, OP3, OP2, OP1, OP0}; ALU_OP[3:0] = in_1; REG_DEST = ALU_SRC; SW = STORE

  // Notes on the sheet:
  //   Tipo I
  //   Tipo R
  //   R
  //   I
  //   Primeira Origem
  //   Segunda Origem
  //   Destino
  //   I
  //   R
  //   Estender bits (Imediato)
  //   LOAD
  //   20b de end
  //   QntMemoria = 2^#end = 2^20 * 4(bytes) = 4MB
endmodule
