// Logisim project meu_circuito.circ as structural Verilog: 2 circuits, main circuit main
module main (
  input  in_1,
  input  in_2,
  input  [3:0] ALU_OP
);

  wire BRANCH, CLK, IE, JMP, LINK, MLE, MSE, WE;
  wire [4:0] multiplexer_4_out, multiplexer_5_out;
  wire [31:0] A, adder_2_out, B, C, imm, jaddr, jimm, mips_ram_1_p7, multiplexer_1_out, multiplexer_2_out,
       multiplexer_3_out, multiplexer_6_out, NEXTPC, OFFSET, OP, PC, res, shifter_1_out, shifter_3_out;

  Adder #(.width(32)) adder_1 (.a(PC), .b(32'h4), .out(NEXTPC));  // open: cin, cout
  Multiplexer #(.width(32)) multiplexer_1 (
    .in0({32{1'b0}}), .in1(OFFSET), .out(multiplexer_1_out), .sel(BRANCH));  // open: en
  // Probe on multiplexer_1_out
  Adder #(.width(32)) adder_2 (.a(NEXTPC), .b(multiplexer_1_out), .out(adder_2_out));  // open: cin, cout
  Multiplexer #(.width(32)) multiplexer_2 (
    .in0(adder_2_out), .in1(jaddr), .out(multiplexer_2_out), .sel(in_2));  // open: en
  // Probe on jaddr
  // MIPSProgramROM mipsprogramrom_1: pin names not known; wires that end beside it: PC, OP
  Register #(.width(32)) register_1 (.D(multiplexer_2_out), .Q(PC), .clk(CLK));  // open: en, clr
  assign imm = {{16{1'b0}}, OP[15:0]};  // Bit_Extender bit_extender_1
  // Probe on imm[26:0]
  Clock clock_1 (.out(CLK));
  assign jimm = {{5{1'b0}}, imm[26:0]};  // Bit_Extender bit_extender_2
  // Probe on jimm
  Multiplexer #(.width(32)) multiplexer_3 (.in0(res), .in1(NEXTPC), .out(multiplexer_3_out), .sel(LINK));  // open: en
  Multiplexer #(.width(5)) multiplexer_4 (
    .in0(OP[15:11]), .in1(OP[20:16]), .out(multiplexer_4_out), .sel(IE));  // open: en
  Multiplexer #(.width(5)) multiplexer_5 (
    .in0(multiplexer_4_out), .in1({5{1'b1}}), .out(multiplexer_5_out), .sel(LINK));  // open: en
  // RegisterFile registerfile_1: pin names not known; wires that end beside it: multiplexer_3_out, CLK, WE, multiplexer_5_out, OP[25:21], OP[20:16], A, B
  Multiplexer #(.width(32)) multiplexer_6 (.in0(B), .in1(imm), .out(multiplexer_6_out), .sel(IE));  // open: en
  // Mips_ALU mips_alu_1: pin names not known; wires that end beside it: A, multiplexer_6_out, ALU_OP, OP[10:6], C
  Shifter #(.width(32), .shift("lr")) shifter_1 (.in(C), .\dist (5'b00010), .out(shifter_1_out));
  // Probe on ALU_OP
  // Probe on OP[5:0]
  // Probe on OP[31:26]
  controle controle_1 (
    .OPCODE(OP[31:26]), .SPECIAL(OP[5:0]), .in_3(ALU_OP), .MLE(MLE), .MSE(MSE), .JMP(JMP), .JMPSET(in_2),
    .LINK(LINK), .WE(WE), .IE(IE));
  // MIPS_RAM mips_ram_1: pin names not known; wires that end beside it: shifter_1_out[19:0], B, MSE, CLK, MLE, 1'b0, mips_ram_1_p7
  and and_1 (BRANCH, C[0], JMP);
  Shifter #(.width(32)) shifter_2 (.in(imm), .\dist (5'b00010), .out(OFFSET));
  Shifter #(.width(32)) shifter_3 (.in(jimm), .\dist (5'b00010), .out(shifter_3_out));
  Multiplexer #(.width(32)) multiplexer_7 (.in0(shifter_3_out), .in1(A), .out(jaddr), .sel(in_1));  // open: en
  Multiplexer #(.width(32)) multiplexer_8 (.in0(C), .in1(mips_ram_1_p7), .out(res), .sel(MLE));  // open: en

  // Other names for the same wires on the sheet: JMPSET = in_2; JR = in_1; SPECIAL[5:0] = OP[5:0];
  //   SHAMT[4:0] = OP[10:6]; rd[4:0] = OP[15:11]; rt[4:0] = OP[20:16]; rs[4:0] = OP[25:21]; OPCODE[5:0] = OP[31:26]

  // Notes on the sheet:
  //   Tipo I
  //   Tipo J
  //   Tipo R
  //   R
  //   LOAD
endmodule

module controle (
  input  [5:0] OPCODE,
  input  [5:0] SPECIAL,
  input  [3:0] in_3,
  output MLE,
  output MSE,
  output JMP,
  output JMPSET,
  output LINK,
  output WE,
  output IE
);

  wire addf_out, ADDIU, ADDU, JMP_t, JR, jrf_out, subf_out, SUBU, tipoR;

  and u_tipoR (tipoR, ~OPCODE[0], ~OPCODE[1], ~OPCODE[2], ~OPCODE[3], ~OPCODE[4], ~OPCODE[5]);  // AND_Gate
  or or_1 (JMP, JMP_t, LINK);
  or or_2 (WE, ADDU, ADDIU, SUBU, MLE);
  or or_3 (IE, ADDIU, MLE, MSE);
  and isADDIU (ADDIU, OPCODE[0], ~OPCODE[1], ~OPCODE[2], OPCODE[3], ~OPCODE[4], ~OPCODE[5]);  // AND_Gate
  and isSW (MSE, OPCODE[0], OPCODE[1], ~OPCODE[2], OPCODE[3], ~OPCODE[4], OPCODE[5]);  // AND_Gate
  and isLW (MLE, OPCODE[0], OPCODE[1], ~OPCODE[2], ~OPCODE[3], ~OPCODE[4], OPCODE[5]);  // AND_Gate
  and isBEQ (JMPSET, ~OPCODE[0], ~OPCODE[1], ~OPCODE[2], ~OPCODE[3], OPCODE[4], ~OPCODE[5]);  // AND_Gate
  and isJ (JMP_t, ~OPCODE[0], OPCODE[1], ~OPCODE[2], ~OPCODE[3], ~OPCODE[4], ~OPCODE[5]);  // AND_Gate
  and isJAL (LINK, OPCODE[0], OPCODE[1], ~OPCODE[2], ~OPCODE[3], ~OPCODE[4], ~OPCODE[5]);  // AND_Gate
  and addf (addf_out, SPECIAL[0], ~SPECIAL[1], ~SPECIAL[2], ~SPECIAL[3], ~SPECIAL[4], SPECIAL[5]);  // AND_Gate
  and and_1 (ADDU, addf_out, tipoR);
  and subf (subf_out, SPECIAL[0], SPECIAL[1], ~SPECIAL[2], ~SPECIAL[3], ~SPECIAL[4], SPECIAL[5]);  // AND_Gate
  and and_2 (SUBU, subf_out, tipoR);
  and jrf (jrf_out, ~SPECIAL[0], ~SPECIAL[1], SPECIAL[2], ~SPECIAL[3], ~SPECIAL[4], ~SPECIAL[5]);  // AND_Gate
  and and_3 (JR, jrf_out, tipoR);

  // Other names for the same wires on the sheet: ALU_OP[3:0] = in_3; BEQ = JMPSET; JAL = LINK; LW = MLE;
  //   OP0 = OPCODE[0]; OP1 = OPCODE[1]; OP2 = OPCODE[2]; OP3 = OPCODE[3]; OP4 = OPCODE[4]; OP5 = OPCODE[5];
  //   F0 = SPECIAL[0]; F1 = SPECIAL[1]; F2 = SPECIAL[2]; F3 = SPECIAL[3]; F4 = SPECIAL[4]; F5 = SPECIAL[5]; SW = MSE

  // Notes on the sheet:
  //   Tipo R  ->  000000
  //   ADDIU  ->  001001
  //   SW -> 101011
  //   LW  ->  100011
  //   BEQ  ->  000100
  //   JMP |  000010
  //   JAL  |  000011
endmodule
