// Logisim project projeto_pc_final.circ as structural Verilog: 2 circuits, main circuit main
module main (
);

  wire BRANCH, CLK, IE, JMP, JR, LINK, MLE, MSE, WE;
  wire [1:0] PCSEL;
  wire [3:0] ALU_OP;
  wire [4:0] multiplexer_4_out, multiplexer_5_out;
  wire [31:0] A, adder_2_out, B, C, imm, jaddr, jimm, mips_ram_1_p7, multiplexer_1_out, multiplexer_2_out,
       multiplexer_3_out, multiplexer_6_out, NEXTPC, OFFSET, OP, PC, res, shifter_1_out, shifter_3_out;

  // Probe on NEXTPC
  Adder #(.width(32)) adder_1 (.a(PC), .b(32'h4), .out(NEXTPC));  // open: cin, cout
  Multiplexer #(.width(32)) multiplexer_1 (
    .in0({32{1'b0}}), .in1(OFFSET), .out(multiplexer_1_out), .sel(BRANCH));  // open: en
  // Probe on multiplexer_1_out
  Clock clock_1 (.out(CLK));
  Adder #(.width(32)) adder_2 (.a(NEXTPC), .b(multiplexer_1_out), .out(adder_2_out));  // open: cin, cout
  Multiplexer #(.select(2), .width(32)) multiplexer_2 (
    .in0(adder_2_out), .in1(jaddr), .in2(A), .out(multiplexer_2_out), .sel(PCSEL));  // open: in3, en
  // Probe on PCSEL
  // MIPSProgramROM mipsprogramrom_1: pin names not known; wires that end beside it: PC, OP
  // Probe on PC
  Register #(.width(32)) register_1 (.D(multiplexer_2_out), .Q(PC), .clk(CLK));  // open: en, clr
  // Probe on jimm
  assign jimm = {{6{1'b0}}, OP[25:0]};  // Bit_Extender bit_extender_1
  assign imm = {{16{1'b0}}, OP[15:0]};  // Bit_Extender bit_extender_2
  // Probe on imm
  // Probe on OP[5:0]
  // Probe on multiplexer_3_out
  Multiplexer #(.width(32)) multiplexer_3 (.in0(res), .in1(NEXTPC), .out(multiplexer_3_out), .sel(LINK));  // open: en
  Multiplexer #(.width(5)) multiplexer_4 (
    .in0(OP[15:11]), .in1(OP[20:16]), .out(multiplexer_4_out), .sel(IE));  // open: en
  Multiplexer #(.width(5)) multiplexer_5 (
    .in0(multiplexer_4_out), .in1({5{1'b1}}), .out(multiplexer_5_out), .sel(LINK));  // open: en
  // Probe on OP[25:21]
  // Probe on A
  // RegisterFile registerfile_1: pin names not known; wires that end beside it: multiplexer_3_out, CLK, WE, multiplexer_5_out, OP[25:21], OP[20:16], A, B
  Multiplexer #(.width(32)) multiplexer_6 (.in0(B), .in1(imm), .out(multiplexer_6_out), .sel(IE));  // open: en
  // Probe on multiplexer_6_out
  Shifter #(.width(32), .shift("lr")) shifter_1 (.in(C), .\dist (5'b00010), .out(shifter_1_out));
  // Probe on A
  // Mips_ALU mips_alu_1: pin names not known; wires that end beside it: A, multiplexer_6_out, ALU_OP, OP[10:6], C
  // Probe on OP[31:26]
  // Probe on OP[5:0]
  // Probe on shifter_1_out[19:0]
  // Probe on ALU_OP
  controle controle_1 (
    .OPCODE(OP[31:26]), .SPECIAL(OP[5:0]), .MLE(MLE), .MSE(MSE), .LINK(LINK), .JMP(JMP), .LINK_2(LINK),
    .PCSEL(PCSEL), .JR(JR), .WE(WE), .IE(IE), .ALU_OP(ALU_OP));
  // MIPS_RAM mips_ram_1: pin names not known; wires that end beside it: shifter_1_out[19:0], B, MSE, CLK, MLE, 1'b0, mips_ram_1_p7
  and and_1 (BRANCH, C[0], JMP);
  Shifter #(.width(32)) shifter_2 (.in(imm), .\dist (5'b00010), .out(OFFSET));
  Shifter #(.width(32)) shifter_3 (.in(jimm), .\dist (5'b00010), .out(shifter_3_out));
  Multiplexer #(.width(32)) multiplexer_7 (.in0(C), .in1(mips_ram_1_p7), .out(res), .sel(MLE));  // open: en
  Multiplexer #(.width(32)) multiplexer_8 (.in0(shifter_3_out), .in1(A), .out(jaddr), .sel(JR));  // open: en

  // Other names for the same wires on the sheet: SPECIAL[5:0] = OP[5:0]; SHAMT[4:0] = OP[10:6]; rd[4:0] = OP[15:11];
  //   rt[4:0] = OP[20:16]; rs[4:0] = OP[25:21]; OPCODE[5:0] = OP[31:26]

  // Notes on the sheet:
  //   Tipo J
  //   R
  //   LOAD
endmodule

module controle (
  input  [5:0] OPCODE,
  input  [5:0] SPECIAL,
  output MLE,
  output MSE,
  output LINK,
  output JMP,
  output LINK_2,
  output [1:0] PCSEL,
  output JR,
  output WE,
  output IE,
  output [3:0] ALU_OP
);

  wire addf_out, ADDIU, ADDU, BEQ, BGTZ, BLEZ, J, jrf_out, SLL, sllf_out, subf_out, SUBU, tipoR;
  wire [2:0] or_7_out;

  or or_1 (JMP, BEQ, BGTZ, BLEZ);
  or or_2 (PCSEL[0], J, LINK);
  and u_tipoR (tipoR, ~OPCODE[0], ~OPCODE[1], ~OPCODE[2], ~OPCODE[3], ~OPCODE[4], ~OPCODE[5]);  // AND_Gate
  or or_3 (IE, ADDIU, MLE, MSE);
  or or_4 (WE, ADDU, ADDIU, LINK, SUBU, MLE, SLL);
  and isADDIU (ADDIU, OPCODE[0], ~OPCODE[1], ~OPCODE[2], OPCODE[3], ~OPCODE[4], ~OPCODE[5]);  // AND_Gate
  and addf (addf_out, SPECIAL[0], ~SPECIAL[1], ~SPECIAL[2], ~SPECIAL[3], ~SPECIAL[4], SPECIAL[5]);  // AND_Gate
  and subf (subf_out, SPECIAL[0], SPECIAL[1], ~SPECIAL[2], ~SPECIAL[3], ~SPECIAL[4], SPECIAL[5]);  // AND_Gate
  and jrf (jrf_out, ~SPECIAL[0], ~SPECIAL[1], ~SPECIAL[2], SPECIAL[3], ~SPECIAL[4], ~SPECIAL[5]);  // AND_Gate
  and sllf (sllf_out, ~SPECIAL[0], ~SPECIAL[1], ~SPECIAL[2], ~SPECIAL[3], ~SPECIAL[4], ~SPECIAL[5]);  // AND_Gate
  and isSW (MSE, OPCODE[0], OPCODE[1], ~OPCODE[2], OPCODE[3], ~OPCODE[4], OPCODE[5]);  // AND_Gate
  and isLW (MLE, OPCODE[0], OPCODE[1], ~OPCODE[2], ~OPCODE[3], ~OPCODE[4], OPCODE[5]);  // AND_Gate
  and isBEQ (BEQ, ~OPCODE[0], ~OPCODE[1], OPCODE[2], ~OPCODE[3], ~OPCODE[4], ~OPCODE[5]);  // AND_Gate
  and isBGTZ (BGTZ, OPCODE[0], OPCODE[1], OPCODE[2], ~OPCODE[3], ~OPCODE[4], ~OPCODE[5]);  // AND_Gate
  and isBLEZ (BLEZ, ~OPCODE[0], OPCODE[1], OPCODE[2], ~OPCODE[3], ~OPCODE[4], ~OPCODE[5]);  // AND_Gate
  and isJ (J, ~OPCODE[0], OPCODE[1], ~OPCODE[2], ~OPCODE[3], ~OPCODE[4], ~OPCODE[5]);  // AND_Gate
  and isJAL (LINK, OPCODE[0], OPCODE[1], ~OPCODE[2], ~OPCODE[3], ~OPCODE[4], ~OPCODE[5]);  // AND_Gate
  and and_1 (ADDU, addf_out, tipoR);
  // Probe on ADDU
  and and_2 (SUBU, subf_out, tipoR);
  // Probe on SUBU
  and and_3 (JR, jrf_out, tipoR);
  // Probe on JR
  and and_4 (SLL, sllf_out, tipoR);
  // Probe on SLL
  or or_5 (or_7_out[1], SUBU, BEQ);
  or or_6 (or_7_out[2], SLL, BGTZ);
  or or_7 (or_7_out[0], ADDIU, ADDU, SUBU, MLE, MSE, BGTZ);
  Multiplexer #(.select(4), .width(4)) multiplexer_1 (
    .in1(4'b0010), .in2(4'b1001), .in3(4'b0110), .in4(4'b0000), .in5(4'b1101), .in8(4'b1111), .out(ALU_OP),
    .sel({BLEZ, or_7_out}));  // open: in0, in6, in7, in9, in10, in11, in12, in13, in14, in15, en

  assign LINK_2 = LINK;
  assign PCSEL[1] = JR;

  // Other names for the same wires on the sheet: ALUOP[3:0] = ALU_OP; JAL = LINK; LW = MLE; OP0 = OPCODE[0];
  //   OP1 = OPCODE[1]; OP2 = OPCODE[2]; OP3 = OPCODE[3]; OP4 = OPCODE[4]; OP5 = OPCODE[5]; F0 = SPECIAL[0];
  //   F1 = SPECIAL[1]; F2 = SPECIAL[2]; F3 = SPECIAL[3]; F4 = SPECIAL[4]; F5 = SPECIAL[5]; SW = MSE

  // Notes on the sheet:
  //   Tipo R  ->  000000
  //   ADDIU  ->  001001
  //   SW -> 101011
  //   LW  ->  100011
  //   BEQ  ->  010000
  //   BGTZ  ->  000111
  //   BLEZ  ->  000110
  //   J -> 000010
  //   JAL  |  000011
  //   OP tipo R
endmodule
